# Fritzing sketch sketch (saved by Fritzing 0.9.9b)
breadboards: 1

parts:
  part = TS-300B interface
  part_2 = TS 300B sensor
  M2 = PH meter with sensor in breadboard [package=THT]
  DS1 = DS18B20 1-Wire Temperature Sensor Probe
  part_3 = tds-sensor-meter-v1.0_1
  part_4 = LCD1602-I2C
  part_5 = Arduino Uno (Rev3) - ICSP
  part_6 = HC-SR04 Ultrasonic Distance Sensor

nets:
  GND: part.Pin_1, part.Pin_8, part_2.Pin_3, M2.pin3, DS1.GND, part_3.pin3, part_4.GND, part_5.GND, part_6.GND
  N1: part.Pin_2, part_5.A2
  VCC: part.Pin_4, M2.pin2, DS1.VDD, part_3.pin2, part_4.VCC, part_5.5V, part_6.VCC
  N2: part.Pin_5, part_2.Pin_1
  N3: part.Pin_6, part_2.Pin_2
  N4: M2.pin1, part_5.A3
  N5: DS1.DQ, part_5.A1
  N6: part_3.pin1, part_5.A0
  N7: part_4.SDA, part_5.A4/SDA
  N8: part_4.SCL, part_5.A5/SCL
  N9: part_5.D6_PWM, part_6.TRIG
  N10: part_5.D7, part_6.ECHO

custom parts:
  TS-300B interface: TS-300B interface.
  TS 300B sensor: TS 300B water turbidity sensor.
  PH meter with sensor in breadboard: DFrobot PH meter (SKU SEN0161)
  : TDS Meter V1.0 Development Board Water Meter Filter Measuring Water Sensor Module.
  LCD1602-I2C: A standard character display, usually with 2x16 characters. Comes in many colors with LCM1602 IIC attached.
  HC-SR04 Ultrasonic Distance Sensor: The HC-SR04 is an ultrasonic distance sensor. It is capable of providing measurement for ranges of 2cm to 400cm. The module operates at 5V.
